// Logisim project Combinational Arithmetic Logic Circuit.circ as structural Verilog: 1 circuit, main circuit main
module main (
);

  wire and_1_out, and_2_out, or_1_out, undriven, undriven_2, undriven_3, xor_1_out;

  xor xor_1 (xor_1_out, undriven, undriven_2);
  and and_1 (and_1_out, undriven, undriven_2);
  and and_2 (and_2_out, xor_1_out, undriven_3);
  or or_1 (or_1_out, and_2_out, and_1_out);
  // Buffer buffer_1 has open pins: in=or_1_out, out=open

  // Notes on the sheet:
  //   a
  //   b
  //   c
  //   Circuit logic combinational aritmetic pentru o functie majoritara pe 3 variable (pb.1, pag.5)
  //   M
  //   In circuit, s-au folosit:
  //   * o poarta XOR echivalent cu expresia logica x = a (+) b
  //   * doua porti AND echivalente cu expresia x = a b
  //   * o poarta OR echivalente a expresiei x = a + b
endmodule
