// Logisim project Decoder Circuit with NOR Gates.circ as structural Verilog: 1 circuit, main circuit main
module main (
);

  wire nor_1_out, nor_2_out, nor_3_out, nor_4_out, not_1_out, not_2_out, undriven, undriven_2;

  not not_1 (not_1_out, undriven);
  not not_2 (not_2_out, undriven_2);
  nor nor_1 (nor_1_out, not_1_out, not_2_out);
  nor nor_2 (nor_2_out, not_1_out, undriven_2);
  nor nor_3 (nor_3_out, undriven, not_2_out);
  nor nor_4 (nor_4_out, undriven, undriven_2);

  // Notes on the sheet:
  //   a
  //   b
  //              a  
  //         a`
  //         b
  //       b`
  //   Circuit decodor construi cu ajutororul portilor NOR.(pb 1, pg.10)
  //   a`b
  //   a`b
  //     ab`
  //   ab
  //   va fi 2^2, adica 4. 
  //   Circuitul are doua intrari, de aici rezultand ca numarul de iesiri
  //   Se poate observa ca intrarea de validare Enable lipseste. 
endmodule
